# Fritzing sketch circuit (saved by Fritzing 0.9.3b)
breadboards: 1

parts:
  VCC1 = Battery
  M1 = DC Motor
  KY-1 = Keyes Relay [package=THT]
  부품2 = FC-28 Soil Hygrometer Module - Probe
  元件2 = FC-28 Soil Hygrometer Module
  Water_Level_Sensor1 = Water Level Sensor
  元件1 = Arduino Uno (Rev3)

nets:
  N1: VCC1.-, M1.pin_1, KY-1.C
  N2: VCC1.+, M1.pin_2, KY-1.NO
  N3: KY-1.signal, 元件1.D13/SCK
  VCC: KY-1.power, Water_Level_Sensor1.VCC, 元件1.5V
  GND: KY-1.ground, 元件2.GND, Water_Level_Sensor1.GND, 元件1.GND
  N4: 부품2.POS, 元件2.NEG
  N5: 부품2.NEG, 元件2.POS
  VCC_2: 元件2.VCC, 元件1.3V3
  N6: 元件2.AO, 元件1.A0
  N7: Water_Level_Sensor1.SIG, 元件1.A1

custom parts:
  Keyes Relay: The Keyes 5V relay module is suitable for SCM development, home appliance control. It uses a 5V~12V TIL control signal which can control DC / AC signal.
  FC-28 Soil Hygrometer Module - Probe: The FC-28 is a soil hygrometer module that uses the Texas Instruments LM393 comparator chip to provide an analog measurement of soil humidity.
  FC-28 Soil Hygrometer Module: The FC-28 is a soil hygrometer module that uses the Texas Instruments LM393 comparator chip to provide an analog measurement of soil humidity. The digital output is high when soil moisture is over a certain threshold, as determined by adjusting the potentiometer.
  Water Level Sensor: A water level sensor. This sensor operates at 3V to 5V. The Sig (signal) pin outputs an analogue signal that is in proportion to the amount of water in contact with the sensor.
